# Fritzing sketch Connection (saved by Fritzing 0.9.3b)
circuit board: 8.46667cm x 5.64444cm
breadboards: 1

parts:
  esp1 = ESP32 DevKitc V4
  DHT1 = Humidity and Temperature Sensor DHT11
  KF-1 = KF-301 Relay [package=THT]
  J2 = Basic Servo
  M3 = DC Motor
  LED1 = RGB LED (com. anode, rbg) [package="5 mm [THT]"]
  J3 = Piezo Speaker
  VCC1 = Battery block 9V
  M4 = fc-51 [package=THT]
  M5 = fc-51 [package=THT]  # not connected
  A1 = Soil Moisture Detection Module

nets:
  GND: esp1.IO18, esp1.GND, DHT1.Data-signal, DHT1.GND_1, KF-1.ground, J2.gnd, M4.pin2, A1.GND
  N1: esp1.IO19, J3.pin1
  N2: esp1.IO21, LED1.green_cathode
  N3: esp1.IO22, LED1.blue_cathode
  N4: esp1.IO23, LED1.red_cathode
  N5: esp1.3V3, LED1.common_anode
  N6: esp1.IO34, A1.DO
  N7: esp1.IO35, M4.pin1
  N8: esp1.IO27, J2.pulse
  N9: esp1.IO13, KF-1.signal
  VCC: esp1.5V, DHT1.Vcc, KF-1.power, J2.vcc, J3.pin2, M4.pin3, A1.VCC
  N10: KF-1.NC, VCC1.-
  N11: KF-1.C, M3.pin_2
  N12: M3.pin_1, VCC1.+

custom parts:
  ESP32 DevKitc V4: ESP32-DevKitC board with ESP32-WROOM-32 module. ESP32-DevKitC V4 is a small-sized ESP32-based development board produced by Espressif. Most of the pins on the ESP module are broken out to the pin headers on the board. The pins D0, D1, D2, D3, CMD and CLK are used internally for communication between ESP32 and SPI flash memory. They are grouped on both sides near the USB connector. Avoid using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
  Humidity and Temperature Sensor DHT11: Digital relative humidity & temperature sensor DHT11
  KF-301 Relay: KF-301
